# Fritzing sketch keypad_membrane-switch-control-pad-and-LEDs (saved by Fritzing 0.9.3b)
breadboards: 1

parts:
  Arduino_-_Slave_2 = Arduino Mega 2560 (Rev3)
  Arduino_-_Slave_1 = Arduino Mega 2560 (Rev3)
  Arduino_2_-_Slave1 = Arduino Mega 2560 (Rev3)  # not connected
  Arduino_2_-_Slave2 = Arduino Mega 2560 (Rev3)  # not connected
  Arduino_-_Master = Arduino Mega 2560 (Rev3)
  R1 = Resistor [tolerance=±5% resistance=750 package="2512 [SMD]"]
  R8 = Resistor [tolerance=±5% resistance=750 package="2512 [SMD]"]
  R9 = Resistor [tolerance=±5% resistance=750 package="2512 [SMD]"]
  R10 = Resistor [tolerance=±5% resistance=750 package="2512 [SMD]"]

nets:
  N1: Arduino_-_Slave_2.D21/SCL, Arduino_-_Slave_1.D21/SCL, Arduino_-_Master.3V3, R9.Pin_0, R10.Pin_0
  N2: Arduino_-_Slave_2.D20/SDA, Arduino_-_Slave_1.D20/SDA, Arduino_-_Slave_1.SDA, R1.Pin_0, R8.Pin_0
  GND: Arduino_-_Slave_2.GND, Arduino_-_Slave_1.GND, Arduino_-_Master.GND
  N3: Arduino_-_Master.D21/SCL, R9.Pin_1, R10.Pin_1
  N4: Arduino_-_Master.D20/SDA, R1.Pin_1, R8.Pin_1

notes:
  USB connect to computer.
  This Arduino also connects to the LEDs
  I used 2 750 Ohm resistors in series because the Fritzing max is 999Ohm. Use 1.5K resistors in real life, or any series that sums to 1.5K.

// code stored in the sketch: membrane-switch-control-pad.ino

